// Digital circuit Memory Controller.dig as structural Verilog
module Memory_Controller (
  input  User_Program,
  input  User_Write,
  input  User_Inspect,
  input  Control_Clock,
  input  Control_MAR_In,
  input  Control_RAM_In,
  input  Control_RAM_Out,
  input  Control_Halt_In,
  output RAM_Write,
  output RAM_Output_Enable,
  output User_Output_Enable,
  output Databus_Output_Enable,
  output Databus_Direction,
  output Halt_Out,
  output MAR_Clock
);

  wire and_1_out, and_2_out, and_3_out, and_4_out, and_5_out, not_1_out, not_2_out, not_3_out, not_4_out,
       not_5_out;

  not not_1 (not_1_out, User_Program);
  not not_2 (not_2_out, User_Write);
  not not_3 (not_3_out, User_Inspect);
  not not_4 (not_4_out, Control_MAR_In);
  not not_5 (not_5_out, Control_RAM_Out);
  and and_1 (and_1_out, Control_RAM_In, not_1_out);
  and and_2 (and_2_out, User_Program, not_2_out);
  and and_3 (and_3_out, Control_RAM_Out, not_1_out);
  and and_4 (and_4_out, not_3_out, User_Program);
  or or_1 (User_Output_Enable, User_Inspect, not_1_out);
  and and_5 (and_5_out, Control_RAM_In, Control_RAM_Out);
  and and_6 (Databus_Direction, not_5_out, not_1_out);
  or or_2 (Halt_Out, Control_Halt_In, User_Program);
  and and_7 (MAR_Clock, not_4_out, Control_Clock);
  or or_3 (RAM_Write, and_1_out, and_2_out);
  or or_4 (RAM_Output_Enable, and_3_out, and_4_out);
  or or_5 (Databus_Output_Enable, and_5_out, User_Program);

  // Notes on the sheet:
  //   RAM_Write: pin 13
  //   RAM_Output_Enable: pin 14
  //   User_Output_Enable: pin 15
  //   Databus_Output_Enable: pin 16
  //   Databus_Direction: pin 17
  //   Halt_Out: pin 18
  //   MAR_Clock: pin 19
  //   User_Program: pin 8
  //   User_Write: pin 9
  //   User_Inspect: pin 7
  //   Control_Clock: pin 2
  //   Control_MAR_In: pin 4
  //   Control_RAM_In: pin 5
  //   Control_RAM_Out: pin 6
  //   Control_Halt_In: pin 3
endmodule
